// Logisim project a5.circ as structural Verilog: 3 circuits, main circuit main
module main (
  input  Mode,
  input  address_bit,
  input  address_bit_2,
  input  address_bit_3,
  input  data_bit,
  input  data_bit_2,
  input  data_bit_3,
  input  data_bit_4,
  output output_bit,
  output output_bit_2,
  output output_bit_3,
  output output_bit_4
);

  wire abs_bits_through_1_out_6, abs_bits_through_1_out_7, abs_bits_through_1_out_8,
       abs_bits_through_1_out_9, abs_bits_through_2_out_6, abs_bits_through_2_out_7,
       abs_bits_through_2_out_8, abs_bits_through_2_out_9, abs_bits_through_3_out_6,
       abs_bits_through_3_out_7, abs_bits_through_3_out_8, abs_bits_through_3_out_9,
       abs_bits_through_4_out_6, abs_bits_through_4_out_7, abs_bits_through_4_out_8,
       abs_bits_through_4_out_9, abs_bits_through_5_out_6, abs_bits_through_5_out_7,
       abs_bits_through_5_out_8, abs_bits_through_5_out_9, abs_bits_through_6_out_6,
       abs_bits_through_6_out_7, abs_bits_through_6_out_8, abs_bits_through_6_out_9,
       abs_bits_through_7_out_6, abs_bits_through_7_out_7, abs_bits_through_7_out_8,
       abs_bits_through_7_out_9, abs_bits_through_8_out_6, abs_bits_through_8_out_7,
       abs_bits_through_8_out_8, abs_bits_through_8_out_9, address_q, and_1_out, and_2_out, and_3_out,
       and_4_out, and_5_out, and_6_out, and_7_out, and_8_out, and_9_out, and_10_out, and_11_out, and_12_out,
       and_13_out, and_14_out, and_15_out, and_16_out, and_17_out, and_18_out, and_19_out, and_20_out,
       and_21_out, and_22_out, and_23_out, and_24_out, clock_out, d_ff_1_q, d_ff_2_q, d_ff_3_q, d_ff_4_q,
       d_ff_5_q, data_in_q, mode_q, not_1_out, not_2_out, not_3_out, not_4_out, onebmem_1_out_7,
       onebmem_1_out_8, onebmem_1_out_9, onebmem_1_out_10, onebmem_2_out_7, onebmem_2_out_8, onebmem_2_out_9,
       onebmem_2_out_10, onebmem_3_out_7, onebmem_3_out_8, onebmem_3_out_9, onebmem_3_out_10,
       onebmem_4_out_7, onebmem_4_out_8, onebmem_4_out_9, onebmem_4_out_10, onebmem_5_out_7, onebmem_5_out_8,
       onebmem_5_out_9, onebmem_5_out_10, onebmem_6_out_7, onebmem_6_out_8, onebmem_6_out_9,
       onebmem_6_out_10, onebmem_7_out_7, onebmem_7_out_8, onebmem_7_out_9, onebmem_7_out_10,
       onebmem_8_out_7, onebmem_8_out_8, onebmem_8_out_9, onebmem_8_out_10, or_1_out, or_2_out, or_3_out,
       or_4_out, or_5_out, or_6_out, or_7_out, or_8_out, or_9_out, or_10_out, or_11_out, or_12_out;

  D_Flip_Flop u_mode (.D(Mode), .clk(clock_out), .Q(mode_q));  // open: Qn, preset, reset
  D_Flip_Flop address (.D(address_bit), .clk(clock_out), .Q(address_q));  // open: Qn, preset, reset
  D_Flip_Flop d_ff_1 (.D(address_bit_2), .clk(clock_out), .Q(d_ff_1_q));  // open: Qn, preset, reset
  D_Flip_Flop d_ff_2 (.D(address_bit_3), .clk(clock_out), .Q(d_ff_2_q));  // open: Qn, preset, reset
  D_Flip_Flop data_in (.D(data_bit), .clk(clock_out), .Q(data_in_q));  // open: Qn, preset, reset
  D_Flip_Flop d_ff_3 (.D(data_bit_2), .clk(clock_out), .Q(d_ff_3_q));  // open: Qn, preset, reset
  D_Flip_Flop d_ff_4 (.D(data_bit_3), .clk(clock_out), .Q(d_ff_4_q));  // open: Qn, preset, reset
  D_Flip_Flop d_ff_5 (.D(data_bit_4), .clk(clock_out), .Q(d_ff_5_q));  // open: Qn, preset, reset
  not not_1 (not_1_out, address_q);
  not not_2 (not_2_out, d_ff_1_q);
  not not_3 (not_3_out, d_ff_2_q);
  Clock clock (.out(clock_out));
  not not_4 (not_4_out, mode_q);
  and and_1 (and_1_out, not_1_out, not_2_out, not_3_out);
  and and_2 (and_2_out, not_1_out, not_2_out, d_ff_2_q);
  and and_3 (and_3_out, not_1_out, d_ff_1_q, not_3_out);
  and and_4 (and_4_out, not_1_out, d_ff_1_q, d_ff_2_q);
  and and_5 (and_5_out, address_q, not_2_out, not_3_out);
  and and_6 (and_6_out, address_q, not_2_out, d_ff_2_q);
  and and_7 (and_7_out, address_q, d_ff_1_q, not_3_out);
  and and_8 (and_8_out, address_q, d_ff_1_q, d_ff_2_q);
  and and_9 (and_9_out, mode_q, and_1_out);
  and and_10 (and_10_out, mode_q, and_2_out);
  and and_11 (and_11_out, mode_q, and_3_out);
  and and_12 (and_12_out, mode_q, and_4_out);
  and and_13 (and_13_out, mode_q, and_5_out);
  and and_14 (and_14_out, mode_q, and_6_out);
  and and_15 (and_15_out, mode_q, and_7_out);
  and and_16 (and_16_out, mode_q, and_8_out);
  onebmem onebmem_1 (
    .selector(and_9_out), .in_2(data_in_q), .in_3(d_ff_3_q), .in_4(d_ff_4_q), .in_5(d_ff_5_q),
    .in_6(clock_out), .out_7(onebmem_1_out_7), .out_8(onebmem_1_out_8), .out_9(onebmem_1_out_9),
    .out_10(onebmem_1_out_10));
  onebmem onebmem_2 (
    .selector(and_10_out), .in_2(data_in_q), .in_3(d_ff_3_q), .in_4(d_ff_4_q), .in_5(d_ff_5_q),
    .in_6(clock_out), .out_7(onebmem_2_out_7), .out_8(onebmem_2_out_8), .out_9(onebmem_2_out_9),
    .out_10(onebmem_2_out_10));
  onebmem onebmem_3 (
    .selector(and_11_out), .in_2(data_in_q), .in_3(d_ff_3_q), .in_4(d_ff_4_q), .in_5(d_ff_5_q),
    .in_6(clock_out), .out_7(onebmem_3_out_7), .out_8(onebmem_3_out_8), .out_9(onebmem_3_out_9),
    .out_10(onebmem_3_out_10));
  onebmem onebmem_4 (
    .selector(and_12_out), .in_2(data_in_q), .in_3(d_ff_3_q), .in_4(d_ff_4_q), .in_5(d_ff_5_q),
    .in_6(clock_out), .out_7(onebmem_4_out_7), .out_8(onebmem_4_out_8), .out_9(onebmem_4_out_9),
    .out_10(onebmem_4_out_10));
  onebmem onebmem_5 (
    .selector(and_13_out), .in_2(data_in_q), .in_3(d_ff_3_q), .in_4(d_ff_4_q), .in_5(d_ff_5_q),
    .in_6(clock_out), .out_7(onebmem_5_out_7), .out_8(onebmem_5_out_8), .out_9(onebmem_5_out_9),
    .out_10(onebmem_5_out_10));
  onebmem onebmem_6 (
    .selector(and_14_out), .in_2(data_in_q), .in_3(d_ff_3_q), .in_4(d_ff_4_q), .in_5(d_ff_5_q),
    .in_6(clock_out), .out_7(onebmem_6_out_7), .out_8(onebmem_6_out_8), .out_9(onebmem_6_out_9),
    .out_10(onebmem_6_out_10));
  onebmem onebmem_7 (
    .selector(and_15_out), .in_2(data_in_q), .in_3(d_ff_3_q), .in_4(d_ff_4_q), .in_5(d_ff_5_q),
    .in_6(clock_out), .out_7(onebmem_7_out_7), .out_8(onebmem_7_out_8), .out_9(onebmem_7_out_9),
    .out_10(onebmem_7_out_10));
  onebmem onebmem_8 (
    .selector(and_16_out), .in_2(data_in_q), .in_3(d_ff_3_q), .in_4(d_ff_4_q), .in_5(d_ff_5_q),
    .in_6(clock_out), .out_7(onebmem_8_out_7), .out_8(onebmem_8_out_8), .out_9(onebmem_8_out_9),
    .out_10(onebmem_8_out_10));
  and and_17 (and_17_out, and_1_out, not_4_out);
  and and_18 (and_18_out, and_2_out, not_4_out);
  and and_19 (and_19_out, and_3_out, not_4_out);
  and and_20 (and_20_out, and_4_out, not_4_out);
  and and_21 (and_21_out, and_5_out, not_4_out);
  and and_22 (and_22_out, and_6_out, not_4_out);
  and and_23 (and_23_out, and_7_out, not_4_out);
  and and_24 (and_24_out, and_8_out, not_4_out);
  abs_bits_through abs_bits_through_1 (
    .selector(and_17_out), .in_2(onebmem_1_out_7), .in_3(onebmem_1_out_8), .in_4(onebmem_1_out_9),
    .in_5(onebmem_1_out_10), .out_6(abs_bits_through_1_out_6), .out_7(abs_bits_through_1_out_7),
    .out_8(abs_bits_through_1_out_8), .out_9(abs_bits_through_1_out_9));
  abs_bits_through abs_bits_through_2 (
    .selector(and_18_out), .in_2(onebmem_2_out_7), .in_3(onebmem_2_out_8), .in_4(onebmem_2_out_9),
    .in_5(onebmem_2_out_10), .out_6(abs_bits_through_2_out_6), .out_7(abs_bits_through_2_out_7),
    .out_8(abs_bits_through_2_out_8), .out_9(abs_bits_through_2_out_9));
  abs_bits_through abs_bits_through_3 (
    .selector(and_19_out), .in_2(onebmem_3_out_7), .in_3(onebmem_3_out_8), .in_4(onebmem_3_out_9),
    .in_5(onebmem_3_out_10), .out_6(abs_bits_through_3_out_6), .out_7(abs_bits_through_3_out_7),
    .out_8(abs_bits_through_3_out_8), .out_9(abs_bits_through_3_out_9));
  abs_bits_through abs_bits_through_4 (
    .selector(and_20_out), .in_2(onebmem_4_out_7), .in_3(onebmem_4_out_8), .in_4(onebmem_4_out_9),
    .in_5(onebmem_4_out_10), .out_6(abs_bits_through_4_out_6), .out_7(abs_bits_through_4_out_7),
    .out_8(abs_bits_through_4_out_8), .out_9(abs_bits_through_4_out_9));
  abs_bits_through abs_bits_through_5 (
    .selector(and_21_out), .in_2(onebmem_5_out_7), .in_3(onebmem_5_out_8), .in_4(onebmem_5_out_9),
    .in_5(onebmem_5_out_10), .out_6(abs_bits_through_5_out_6), .out_7(abs_bits_through_5_out_7),
    .out_8(abs_bits_through_5_out_8), .out_9(abs_bits_through_5_out_9));
  abs_bits_through abs_bits_through_6 (
    .selector(and_22_out), .in_2(onebmem_6_out_7), .in_3(onebmem_6_out_8), .in_4(onebmem_6_out_9),
    .in_5(onebmem_6_out_10), .out_6(abs_bits_through_6_out_6), .out_7(abs_bits_through_6_out_7),
    .out_8(abs_bits_through_6_out_8), .out_9(abs_bits_through_6_out_9));
  abs_bits_through abs_bits_through_7 (
    .selector(and_23_out), .in_2(onebmem_7_out_7), .in_3(onebmem_7_out_8), .in_4(onebmem_7_out_9),
    .in_5(onebmem_7_out_10), .out_6(abs_bits_through_7_out_6), .out_7(abs_bits_through_7_out_7),
    .out_8(abs_bits_through_7_out_8), .out_9(abs_bits_through_7_out_9));
  abs_bits_through abs_bits_through_8 (
    .selector(and_24_out), .in_2(onebmem_8_out_7), .in_3(onebmem_8_out_8), .in_4(onebmem_8_out_9),
    .in_5(onebmem_8_out_10), .out_6(abs_bits_through_8_out_6), .out_7(abs_bits_through_8_out_7),
    .out_8(abs_bits_through_8_out_8), .out_9(abs_bits_through_8_out_9));
  or or_1 (or_1_out, abs_bits_through_1_out_6, abs_bits_through_2_out_6, abs_bits_through_3_out_6, abs_bits_through_4_out_6);
  or or_2 (or_2_out, abs_bits_through_1_out_7, abs_bits_through_2_out_7, abs_bits_through_3_out_7, abs_bits_through_4_out_7);
  or or_3 (or_3_out, abs_bits_through_1_out_8, abs_bits_through_2_out_8, abs_bits_through_3_out_8, abs_bits_through_4_out_8);
  or or_4 (or_4_out, abs_bits_through_1_out_9, abs_bits_through_2_out_9, abs_bits_through_3_out_9, abs_bits_through_4_out_9);
  or or_5 (or_5_out, abs_bits_through_5_out_6, abs_bits_through_6_out_6, abs_bits_through_7_out_6, abs_bits_through_8_out_6);
  or or_6 (or_6_out, abs_bits_through_5_out_7, abs_bits_through_6_out_7, abs_bits_through_7_out_7, abs_bits_through_8_out_7);
  or or_7 (or_7_out, abs_bits_through_5_out_8, abs_bits_through_6_out_8, abs_bits_through_7_out_8, abs_bits_through_8_out_8);
  or or_8 (or_8_out, abs_bits_through_5_out_9, abs_bits_through_6_out_9, abs_bits_through_7_out_9, abs_bits_through_8_out_9);
  or or_9 (or_9_out, or_1_out, or_5_out);
  or or_10 (or_10_out, or_2_out, or_6_out);
  or or_11 (or_11_out, or_3_out, or_7_out);
  or or_12 (or_12_out, or_4_out, or_8_out);
  D_Flip_Flop #(.trigger("falling")) d_ff_6 (.D(or_9_out), .clk(clock_out), .Q(output_bit));  // open: Qn, preset, reset
  D_Flip_Flop #(.trigger("falling")) d_ff_7 (
    .D(or_10_out), .clk(clock_out), .Q(output_bit_2));  // open: Qn, preset, reset
  D_Flip_Flop #(.trigger("falling")) d_ff_8 (
    .D(or_11_out), .clk(clock_out), .Q(output_bit_3));  // open: Qn, preset, reset
  D_Flip_Flop #(.trigger("falling")) d_ff_9 (
    .D(or_12_out), .clk(clock_out), .Q(output_bit_4));  // open: Qn, preset, reset

  // Notes on the sheet:
  //   D0
  //   D1
  //   D2
  //   D3
  //   D4
  //   D5
  //   D6
  //   D7
endmodule

module onebmem (
  input  selector,
  input  in_2,
  input  in_3,
  input  in_4,
  input  in_5,
  input  in_6,
  output out_7,
  output out_8,
  output out_9,
  output out_10
);

  wire and_1_out, and_2_out, and_3_out, and_4_out, and_5_out, and_6_out, and_7_out, and_8_out, not_1_out,
       not_2_out, not_3_out, not_4_out, or_1_out, or_2_out, or_3_out, or_4_out;

  not not_1 (not_1_out, selector);
  not not_2 (not_2_out, selector);
  not not_3 (not_3_out, selector);
  not not_4 (not_4_out, selector);
  and and_1 (and_1_out, not_2_out, out_7);
  and and_2 (and_2_out, selector, in_2);
  and and_3 (and_3_out, not_3_out, out_8);
  and and_4 (and_4_out, selector, in_3);
  and and_5 (and_5_out, not_4_out, out_9);
  and and_6 (and_6_out, selector, in_4);
  and and_7 (and_7_out, not_1_out, out_10);
  and and_8 (and_8_out, selector, in_5);
  or or_1 (or_1_out, and_1_out, and_2_out);
  or or_2 (or_2_out, and_3_out, and_4_out);
  or or_3 (or_3_out, and_5_out, and_6_out);
  or or_4 (or_4_out, and_7_out, and_8_out);
  D_Flip_Flop #(.trigger("falling")) d_ff_1 (.D(or_4_out), .clk(in_6), .Q(out_10));  // open: Qn, preset, reset
  D_Flip_Flop #(.trigger("falling")) d_ff_2 (.D(or_1_out), .clk(in_6), .Q(out_7));  // open: Qn, preset, reset
  D_Flip_Flop #(.trigger("falling")) d_ff_3 (.D(or_2_out), .clk(in_6), .Q(out_8));  // open: Qn, preset, reset
  D_Flip_Flop #(.trigger("falling")) d_ff_4 (.D(or_3_out), .clk(in_6), .Q(out_9));  // open: Qn, preset, reset

  // Notes on the sheet:
  //   One nibble memory cell
endmodule

// bits_through
module abs_bits_through (
  input  selector,
  input  in_2,
  input  in_3,
  input  in_4,
  input  in_5,
  output out_6,
  output out_7,
  output out_8,
  output out_9
);

  and and_1 (out_6, selector, in_2);
  and and_2 (out_7, selector, in_3);
  and and_3 (out_8, selector, in_4);
  and and_4 (out_9, selector, in_5);

  // Notes on the sheet:
  //   Displays bits if selected, else 0000
endmodule
