// Logisim project a6.circ as structural Verilog: 3 circuits, main circuit main
module main (
  input  in_1,
  input  in_2,
  input  in_3,
  input  in_4,
  input  in_5,
  input  in_6,
  input  in_7,
  input  in_8,
  input  in_9,
  output Bit2_overflow,
  output Bit1_negative,
  output Bit0_zero,
  output out_13,
  output out_14,
  output out_15,
  output out_16
);

  wire ADD_1_out_6, ADD_1_out_7, ADD_1_out_8, ADD_1_out_9, and_1_out, and_2_out, and_3_out, and_4_out,
       and_5_out, and_6_out, and_7_out, and_8_out, and_9_out, and_10_out, clock_1_out, d_ff_1_q, d_ff_2_q,
       d_ff_3_q, d_ff_4_q, d_ff_5_q, d_ff_6_q, d_ff_7_q, d_ff_8_q, d_ff_9_q, full_adder_1_c_out,
       full_adder_2_c_out, full_adder_3_c_out, minminpl_out, minplmin_out, not_1_out, not_2_out, not_3_out,
       not_4_out, not_5_out, not_6_out, not_7_out, not_8_out, not_9_out, not_10_out, not_11_out, not_12_out,
       not_13_out, not_14_out, not_15_out, not_16_out, not_17_out, or_1_out, or_2_out, or_3_out,
       plminmin_out, plplpl_out, xor_1_out, xor_3_out, xor_4_out, xor_5_out, xor_6_out, xor_7_out;

  Clock clock_1 (.out(clock_1_out));
  D_Flip_Flop d_ff_1 (.D(in_9), .clk(clock_1_out), .Q(d_ff_1_q));  // open: Qn, preset, reset
  not not_1 (not_1_out, d_ff_1_q);
  D_Flip_Flop d_ff_2 (.D(in_1), .clk(clock_1_out), .Q(d_ff_2_q));  // open: Qn, preset, reset
  full_adder full_adder_1 (
    .c_out(full_adder_1_c_out), .in_1(d_ff_2_q), .in_2(xor_1_out), .sum(out_13), .c_in(full_adder_2_c_out));
  D_Flip_Flop d_ff_3 (.D(in_2), .clk(clock_1_out), .Q(d_ff_3_q));  // open: Qn, preset, reset
  D_Flip_Flop d_ff_4 (.D(in_3), .clk(clock_1_out), .Q(d_ff_4_q));  // open: Qn, preset, reset
  full_adder full_adder_2 (
    .c_out(full_adder_2_c_out), .in_1(d_ff_3_q), .in_2(xor_4_out), .sum(out_14), .c_in(full_adder_3_c_out));
  D_Flip_Flop d_ff_5 (.D(in_4), .clk(clock_1_out), .Q(d_ff_5_q));  // open: Qn, preset, reset
  full_adder full_adder_3 (
    .c_out(full_adder_3_c_out), .in_1(d_ff_4_q), .in_2(xor_3_out), .sum(out_15), .c_in(and_1_out));
  not not_2 (not_2_out, out_13);
  not not_3 (not_3_out, out_15);
  and and_1 (and_1_out, d_ff_5_q, xor_5_out);
  not not_4 (not_4_out, out_14);
  not not_5 (not_5_out, out_16);
  and and_2 (and_2_out, not_1_out, d_ff_6_q);
  xor xor_1 (xor_1_out, and_2_out, ADD_1_out_6);
  xor xor_2 (out_16, d_ff_5_q, xor_5_out);
  and and_3 (and_3_out, not_2_out, not_4_out, not_3_out, not_5_out);
  D_Flip_Flop d_ff_6 (.D(in_5), .clk(clock_1_out), .Q(d_ff_6_q));  // open: Qn, preset, reset
  and and_4 (and_4_out, not_1_out, d_ff_7_q);
  and and_5 (and_5_out, not_1_out, d_ff_8_q);
  xor xor_3 (xor_3_out, and_5_out, ADD_1_out_8);
  xor xor_4 (xor_4_out, and_4_out, ADD_1_out_7);
  and and_6 (and_6_out, not_1_out, d_ff_9_q);
  xor xor_5 (xor_5_out, and_6_out, ADD_1_out_9);
  D_Flip_Flop d_ff_7 (.D(in_6), .clk(clock_1_out), .Q(d_ff_7_q));  // open: Qn, preset, reset
  D_Flip_Flop d_ff_8 (.D(in_7), .clk(clock_1_out), .Q(d_ff_8_q));  // open: Qn, preset, reset
  and and_7 (and_7_out, d_ff_1_q, d_ff_6_q);
  not not_6 (not_6_out, and_7_out);
  not not_7 (not_7_out, d_ff_6_q);
  and plplpl (plplpl_out, not_1_out, not_7_out, not_8_out, out_13);
  not not_8 (not_8_out, d_ff_2_q);
  not not_9 (not_9_out, out_13);
  and minplmin (minplmin_out, not_1_out, full_adder_1_c_out, not_9_out, d_ff_6_q, d_ff_2_q);
  and minminpl (minminpl_out, d_ff_2_q, d_ff_1_q, not_10_out, not_11_out, full_adder_1_c_out);
  not not_10 (not_10_out, out_13);
  not not_11 (not_11_out, d_ff_6_q);
  and plminmin (plminmin_out, d_ff_1_q, out_13, d_ff_6_q, not_12_out);
  not not_12 (not_12_out, d_ff_2_q);
  D_Flip_Flop d_ff_9 (.D(in_8), .clk(clock_1_out), .Q(d_ff_9_q));  // open: Qn, preset, reset
  and and_8 (and_8_out, d_ff_1_q, d_ff_8_q);
  and and_9 (and_9_out, d_ff_1_q, d_ff_7_q);
  not not_13 (not_13_out, and_9_out);
  not not_14 (not_14_out, and_8_out);
  add1 ADD_1 (
    .in_1(not_6_out), .in_2(not_13_out), .in_3(not_14_out), .ALWAYS_1(not_15_out), .in_5(or_1_out),
    .out_6(ADD_1_out_6), .out_7(ADD_1_out_7), .out_8(ADD_1_out_8), .out_9(ADD_1_out_9));
  and and_10 (and_10_out, d_ff_1_q, d_ff_9_q);
  not not_15 (not_15_out, and_10_out);
  not not_16 (not_16_out, plminmin_out);
  not not_17 (not_17_out, plplpl_out);
  or or_1 (or_1_out, not_1_out, d_ff_1_q);
  or or_2 (or_2_out, plplpl_out, minplmin_out, minminpl_out, plminmin_out);
  xor xor_6 (xor_6_out, not_16_out, not_17_out);
  xor xor_7 (xor_7_out, xor_6_out, out_13);
  or or_3 (or_3_out, minplmin_out, minminpl_out, xor_7_out);
  D_Flip_Flop #(.trigger("falling")) d_ff_10 (
    .D(or_2_out), .clk(clock_1_out), .Q(Bit2_overflow));  // open: Qn, preset, reset
  D_Flip_Flop #(.trigger("falling")) d_ff_11 (
    .D(or_3_out), .clk(clock_1_out), .Q(Bit1_negative));  // open: Qn, preset, reset
  D_Flip_Flop #(.trigger("falling")) d_ff_12 (
    .D(and_3_out), .clk(clock_1_out), .Q(Bit0_zero));  // open: Qn, preset, reset

  // Notes on the sheet:
  //   ADD/SUB COMMAND
  //   LEFT INPUT
  //   A-OUT
  //   LEFT TO RIGHT: +, -, CARRY OUT, MSB L, MSB R, MSB AOUT
  //   RIGHT INPUT
  //   STATUS OUTPUT
endmodule

module add1 (
  input  in_1,
  input  in_2,
  input  in_3,
  input  ALWAYS_1,
  input  in_5,
  output out_6,
  output out_7,
  output out_8,
  output out_9
);

  wire and_1_out, and_2_out, and_3_out;

  xor xor_1 (out_6, in_1, and_1_out);
  and and_1 (and_1_out, and_2_out, in_2);
  xor xor_2 (out_7, and_2_out, in_2);
  and and_2 (and_2_out, and_3_out, in_3);
  xor xor_3 (out_8, and_3_out, in_3);
  and and_3 (and_3_out, ALWAYS_1, in_5);
  xor xor_4 (out_9, ALWAYS_1, in_5);
endmodule

module full_adder (
  input  in_1,
  input  in_2,
  input  c_in,
  output c_out,
  output sum
);

  wire and_1_out, and_2_out, xor_1_out;

  and and_1 (and_1_out, in_2, in_1);
  and and_2 (and_2_out, xor_1_out, c_in);
  or or_1 (c_out, and_2_out, and_1_out);
  xor xor_1 (xor_1_out, in_1, in_2);
  xor xor_2 (sum, xor_1_out, c_in);
endmodule
