// Logisim project finprojZ.circ as structural Verilog: 1 circuit, main circuit main
module main (
  input  in_1,
  input  in_2,
  input  in_3,
  input  in_4,
  input  in_5
);

  wire and_1_out, and_2_out, and_3_out, and_4_out, and_5_out, and_6_out, and_7_out, and_8_out, and_9_out,
       and_10_out, and_11_out, and_12_out, and_13_out, and_14_out, and_15_out, and_16_out, and_17_out,
       and_18_out, and_19_out, and_20_out, and_21_out, and_22_out, and_23_out, and_24_out, and_25_out,
       and_26_out, and_27_out, and_28_out, and_29_out, and_30_out, and_31_out, and_32_out, and_33_out,
       and_34_out, and_35_out, and_36_out, and_37_out, and_38_out, and_39_out, and_40_out, and_41_out,
       and_42_out, and_43_out, and_44_out, and_45_out, and_46_out, and_47_out, and_48_out, and_49_out,
       and_50_out, and_51_out, and_52_out, and_53_out, and_54_out, and_55_out, and_56_out, and_57_out,
       and_58_out, and_59_out, and_60_out, and_61_out, and_62_out, and_63_out, and_64_out, and_65_out,
       and_66_out, and_67_out, and_68_out, and_69_out, and_70_out, and_71_out, and_72_out, and_73_out,
       and_74_out, and_75_out, and_76_out, and_77_out, and_78_out, and_79_out, and_80_out, and_81_out,
       and_82_out, and_83_out, and_84_out, and_85_out, and_86_out, and_87_out, and_88_out, and_89_out,
       and_90_out, and_91_out, and_92_out, and_93_out, and_94_out, and_95_out, and_96_out, and_97_out,
       and_98_out, and_99_out, and_100_out, and_101_out, and_102_out, and_103_out, and_104_out, and_105_out,
       and_106_out, and_107_out, and_108_out, and_109_out, and_110_out, and_111_out, and_112_out,
       and_113_out, and_114_out, and_115_out, and_116_out, and_117_out, and_118_out, and_119_out,
       and_120_out, and_121_out, and_122_out, and_123_out, and_124_out, and_125_out, and_126_out,
       and_127_out, and_128_out, and_129_out, and_130_out, and_131_out, and_132_out, and_133_out,
       and_134_out, and_135_out, and_136_out, and_137_out, and_138_out, and_139_out, and_140_out,
       and_141_out, and_142_out, and_143_out, and_144_out, and_145_out, and_146_out, clock_1_out, d_ff_1_q,
       d_ff_2_q, d_ff_3_q, d_ff_4_q, d_ff_5_q, d_ff_6_q, d_ff_7_q, d_ff_8_q, d_ff_9_q, d_ff_10_q, d_ff_11_q,
       d_ff_12_q, d_ff_13_q, d_ff_14_q, d_ff_15_q, d_ff_16_q, d_ff_17_q, d_ff_18_q, d_ff_19_q, d_ff_20_q,
       d_ff_21_q, d_ff_22_q, d_ff_23_q, d_ff_24_q, d_ff_25_q, d_ff_26_q, d_ff_27_q, d_ff_28_q, d_ff_29_q,
       d_ff_30_q, d_ff_31_q, d_ff_32_q, d_ff_33_q, d_ff_34_q, d_ff_35_q, d_ff_36_q, d_ff_37_q, d_ff_38_q,
       d_ff_39_q, d_ff_40_q, d_ff_41_q, d_ff_42_q, d_ff_43_q, d_ff_44_q, d_ff_45_q, d_ff_46_q, d_ff_47_q,
       d_ff_48_q, d_ff_49_q, d_ff_50_q, d_ff_51_q, d_ff_52_q, d_ff_53_q, d_ff_54_q, d_ff_55_q, d_ff_56_q,
       d_ff_57_q, d_ff_58_q, d_ff_59_q, d_ff_60_q, not_1_out, not_2_out, not_3_out, not_4_out, not_5_out,
       not_6_out, not_7_out, not_8_out, not_9_out, not_10_out, not_11_out, not_12_out, not_13_out,
       not_14_out, not_15_out, not_16_out, not_17_out, not_18_out, not_19_out, not_20_out, not_21_out,
       not_22_out, not_23_out, not_24_out, not_25_out, not_26_out, not_27_out, not_28_out, not_29_out,
       not_30_out, not_31_out, not_32_out, not_33_out, not_34_out, not_35_out, not_36_out, not_37_out,
       not_38_out, not_39_out, not_40_out, not_41_out, not_42_out, not_43_out, not_44_out, not_45_out,
       not_46_out, or_1_out, or_2_out, or_3_out, or_4_out, or_5_out, or_6_out, or_7_out, or_8_out, or_9_out,
       or_10_out, or_11_out, or_12_out, or_13_out, or_14_out, or_15_out, or_16_out, or_17_out, or_18_out,
       or_19_out, or_20_out, or_21_out, or_22_out, undriven, undriven_2, undriven_3, undriven_4, undriven_5,
       undriven_6, undriven_7, undriven_8, undriven_9, undriven_10, undriven_11, undriven_12, xor_1_out,
       xor_2_out, xor_3_out, xor_4_out, xor_5_out, xor_6_out, xor_7_out, xor_8_out, xor_9_out, xor_10_out,
       xor_11_out;

  D_Flip_Flop #(.trigger("falling")) d_ff_1 (
    .D(xor_1_out), .clk(clock_1_out), .Q(d_ff_1_q));  // open: Qn, preset, reset
  xor xor_1 (xor_1_out, and_1_out, d_ff_1_q);
  and and_1 (and_1_out, d_ff_2_q, and_2_out);
  D_Flip_Flop #(.trigger("falling")) d_ff_2 (
    .D(xor_2_out), .clk(clock_1_out), .Q(d_ff_2_q));  // open: Qn, preset, reset
  Clock clock_1 (.out(clock_1_out));
  not not_1 (not_1_out, d_ff_3_q);
  not not_2 (not_2_out, d_ff_2_q);
  not not_3 (not_3_out, d_ff_2_q);
  not not_4 (not_4_out, d_ff_3_q);
  not not_5 (not_5_out, d_ff_1_q);
  not not_6 (not_6_out, d_ff_1_q);
  not not_7 (not_7_out, d_ff_3_q);
  not not_8 (not_8_out, d_ff_1_q);
  not not_9 (not_9_out, d_ff_2_q);
  not not_10 (not_10_out, d_ff_1_q);
  not not_11 (not_11_out, d_ff_2_q);
  not not_12 (not_12_out, d_ff_3_q);
  D_Flip_Flop #(.trigger("falling")) d_ff_3 (
    .D(xor_3_out), .clk(clock_1_out), .Q(d_ff_3_q));  // open: Qn, preset, reset
  xor xor_2 (xor_2_out, and_2_out, d_ff_2_q);
  and and_2 (and_2_out, not_14_out, d_ff_3_q);
  and and_3 (and_3_out, d_ff_1_q, d_ff_2_q, clock_1_out, d_ff_3_q);
  and and_4 (and_4_out, d_ff_1_q, d_ff_2_q, clock_1_out, not_1_out);
  and and_5 (and_5_out, d_ff_1_q, not_2_out, clock_1_out, d_ff_3_q);
  and and_6 (and_6_out, d_ff_1_q, not_3_out, clock_1_out, not_4_out);
  and and_7 (and_7_out, not_5_out, d_ff_2_q, clock_1_out, d_ff_3_q);
  and and_8 (and_8_out, not_6_out, d_ff_2_q, clock_1_out, not_7_out);
  and and_9 (and_9_out, not_8_out, not_9_out, clock_1_out, d_ff_3_q);
  and and_10 (and_10_out, not_10_out, not_11_out, clock_1_out, not_12_out);
  and and_11 (and_11_out, and_3_out, not_13_out);
  and and_12 (and_12_out, and_4_out, not_13_out);
  and and_13 (and_13_out, and_5_out, not_13_out);
  and and_14 (and_14_out, and_6_out, not_13_out);
  and and_15 (and_15_out, and_7_out, not_13_out);
  and and_16 (and_16_out, and_8_out, not_13_out);
  and and_17 (and_17_out, and_9_out, not_13_out);
  and and_18 (and_18_out, and_10_out, not_13_out);
  not not_13 (not_13_out, d_ff_4_q);
  D_Flip_Flop #(.trigger("falling")) d_ff_4 (.D(in_1), .clk(clock_1_out), .Q(d_ff_4_q));  // open: Qn, preset, reset
  xor xor_3 (xor_3_out, d_ff_3_q, not_14_out);
  not not_14 (not_14_out, and_86_out);
  D_Flip_Flop #(.trigger("high")) d_ff_5 (.D(and_19_out), .clk(and_11_out), .Q(d_ff_5_q));  // open: Qn, preset, reset
  and and_19 (and_19_out, and_3_out, not_13_out, d_ff_13_q);
  D_Flip_Flop #(.trigger("high")) d_ff_6 (.D(and_20_out), .clk(and_12_out), .Q(d_ff_6_q));  // open: Qn, preset, reset
  and and_20 (and_20_out, and_4_out, not_13_out, d_ff_13_q);
  and and_21 (and_21_out, and_5_out, not_13_out, d_ff_13_q);
  D_Flip_Flop #(.trigger("high")) d_ff_7 (.D(and_21_out), .clk(and_13_out), .Q(d_ff_7_q));  // open: Qn, preset, reset
  and and_22 (and_22_out, and_6_out, not_13_out, d_ff_13_q);
  D_Flip_Flop #(.trigger("high")) d_ff_8 (.D(and_22_out), .clk(and_14_out), .Q(d_ff_8_q));  // open: Qn, preset, reset
  D_Flip_Flop #(.trigger("high")) d_ff_9 (.D(and_23_out), .clk(and_15_out), .Q(d_ff_9_q));  // open: Qn, preset, reset
  and and_23 (and_23_out, and_7_out, not_13_out, d_ff_13_q);
  D_Flip_Flop #(.trigger("high")) d_ff_10 (.D(and_24_out), .clk(and_16_out), .Q(d_ff_10_q));  // open: Qn, preset, reset
  and and_24 (and_24_out, and_8_out, not_13_out, d_ff_13_q);
  and and_25 (and_25_out, and_9_out, not_13_out, d_ff_13_q);
  D_Flip_Flop #(.trigger("high")) d_ff_11 (.D(and_25_out), .clk(and_17_out), .Q(d_ff_11_q));  // open: Qn, preset, reset
  D_Flip_Flop #(.trigger("high")) d_ff_12 (.D(and_26_out), .clk(and_18_out), .Q(d_ff_12_q));  // open: Qn, preset, reset
  and and_26 (and_26_out, and_10_out, not_13_out, d_ff_13_q);
  or or_1 (or_1_out, and_27_out, and_28_out, and_29_out, and_30_out, and_31_out, and_32_out, and_33_out, and_34_out);
  and and_27 (and_27_out, d_ff_5_q, and_3_out, d_ff_4_q);
  and and_28 (and_28_out, d_ff_6_q, and_4_out, d_ff_4_q);
  and and_29 (and_29_out, d_ff_7_q, and_5_out, d_ff_4_q);
  and and_30 (and_30_out, d_ff_8_q, and_6_out, d_ff_4_q);
  and and_31 (and_31_out, d_ff_9_q, and_7_out, d_ff_4_q);
  and and_32 (and_32_out, d_ff_10_q, and_8_out, d_ff_4_q);
  and and_33 (and_33_out, d_ff_11_q, and_9_out, d_ff_4_q);
  and and_34 (and_34_out, d_ff_12_q, and_10_out, d_ff_4_q);
  D_Flip_Flop #(.trigger("falling")) d_ff_13 (.D(in_2), .clk(clock_1_out), .Q(d_ff_13_q));  // open: Qn, preset, reset
  D_Flip_Flop #(.trigger("falling")) d_ff_14 (.D(in_3), .clk(clock_1_out), .Q(d_ff_14_q));  // open: Qn, preset, reset
  D_Flip_Flop #(.trigger("high")) d_ff_15 (.D(and_35_out), .clk(and_11_out), .Q(d_ff_15_q));  // open: Qn, preset, reset
  and and_35 (and_35_out, and_3_out, not_13_out, d_ff_14_q);
  and and_36 (and_36_out, and_4_out, not_13_out, d_ff_14_q);
  D_Flip_Flop #(.trigger("high")) d_ff_16 (.D(and_36_out), .clk(and_12_out), .Q(d_ff_16_q));  // open: Qn, preset, reset
  and and_37 (and_37_out, and_5_out, not_13_out, d_ff_14_q);
  D_Flip_Flop #(.trigger("high")) d_ff_17 (.D(and_37_out), .clk(and_13_out), .Q(d_ff_17_q));  // open: Qn, preset, reset
  D_Flip_Flop #(.trigger("high")) d_ff_18 (.D(and_38_out), .clk(and_14_out), .Q(d_ff_18_q));  // open: Qn, preset, reset
  and and_38 (and_38_out, and_6_out, not_13_out, d_ff_14_q);
  and and_39 (and_39_out, and_7_out, not_13_out, d_ff_14_q);
  D_Flip_Flop #(.trigger("high")) d_ff_19 (.D(and_39_out), .clk(and_15_out), .Q(d_ff_19_q));  // open: Qn, preset, reset
  D_Flip_Flop #(.trigger("high")) d_ff_20 (.D(and_40_out), .clk(and_16_out), .Q(d_ff_20_q));  // open: Qn, preset, reset
  and and_40 (and_40_out, and_8_out, not_13_out, d_ff_14_q);
  and and_41 (and_41_out, and_9_out, not_13_out, d_ff_14_q);
  D_Flip_Flop #(.trigger("high")) d_ff_21 (.D(and_41_out), .clk(and_17_out), .Q(d_ff_21_q));  // open: Qn, preset, reset
  and and_42 (and_42_out, and_10_out, not_13_out, d_ff_14_q);
  D_Flip_Flop #(.trigger("high")) d_ff_22 (.D(and_42_out), .clk(and_18_out), .Q(d_ff_22_q));  // open: Qn, preset, reset
  D_Flip_Flop #(.trigger("falling")) d_ff_23 (.D(in_4), .clk(clock_1_out), .Q(d_ff_23_q));  // open: Qn, preset, reset
  D_Flip_Flop #(.trigger("high")) d_ff_24 (.D(or_1_out), .clk(clock_1_out), .Q(d_ff_24_q));  // open: Qn, preset, reset
  and and_43 (and_43_out, d_ff_15_q, and_3_out, d_ff_4_q);
  and and_44 (and_44_out, d_ff_16_q, and_4_out, d_ff_4_q);
  and and_45 (and_45_out, d_ff_17_q, and_5_out, d_ff_4_q);
  and and_46 (and_46_out, d_ff_18_q, and_6_out, d_ff_4_q);
  and and_47 (and_47_out, d_ff_19_q, and_7_out, d_ff_4_q);
  and and_48 (and_48_out, d_ff_20_q, and_8_out, d_ff_4_q);
  and and_49 (and_49_out, d_ff_21_q, and_9_out, d_ff_4_q);
  and and_50 (and_50_out, d_ff_22_q, and_10_out, d_ff_4_q);
  D_Flip_Flop #(.trigger("falling")) d_ff_25 (.D(in_5), .clk(clock_1_out), .Q(d_ff_25_q));  // open: Qn, preset, reset
  D_Flip_Flop #(.trigger("high")) d_ff_26 (.D(or_2_out), .clk(clock_1_out), .Q(d_ff_26_q));  // open: Qn, preset, reset
  or or_2 (or_2_out, and_43_out, and_44_out, and_45_out, and_46_out, and_47_out, and_48_out, and_49_out, and_50_out);
  D_Flip_Flop #(.trigger("high")) d_ff_27 (.D(or_3_out), .clk(clock_1_out), .Q(d_ff_27_q));  // open: Qn, preset, reset
  D_Flip_Flop #(.trigger("high")) d_ff_28 (.D(or_4_out), .clk(clock_1_out), .Q(d_ff_28_q));  // open: Qn, preset, reset
  and and_51 (and_51_out, and_3_out, not_13_out, d_ff_23_q);
  D_Flip_Flop #(.trigger("high")) d_ff_29 (.D(and_51_out), .clk(and_11_out), .Q(d_ff_29_q));  // open: Qn, preset, reset
  and and_52 (and_52_out, and_4_out, not_13_out, d_ff_23_q);
  D_Flip_Flop #(.trigger("high")) d_ff_30 (.D(and_52_out), .clk(and_12_out), .Q(d_ff_30_q));  // open: Qn, preset, reset
  and and_53 (and_53_out, and_5_out, not_13_out, d_ff_23_q);
  D_Flip_Flop #(.trigger("high")) d_ff_31 (.D(and_53_out), .clk(and_13_out), .Q(d_ff_31_q));  // open: Qn, preset, reset
  D_Flip_Flop #(.trigger("high")) d_ff_32 (.D(and_54_out), .clk(and_14_out), .Q(d_ff_32_q));  // open: Qn, preset, reset
  and and_54 (and_54_out, and_6_out, not_13_out, d_ff_23_q);
  D_Flip_Flop #(.trigger("high")) d_ff_33 (.D(and_55_out), .clk(and_15_out), .Q(d_ff_33_q));  // open: Qn, preset, reset
  and and_55 (and_55_out, and_7_out, not_13_out, d_ff_23_q);
  D_Flip_Flop #(.trigger("high")) d_ff_34 (.D(and_56_out), .clk(and_16_out), .Q(d_ff_34_q));  // open: Qn, preset, reset
  and and_56 (and_56_out, and_8_out, not_13_out, d_ff_23_q);
  D_Flip_Flop #(.trigger("high")) d_ff_35 (.D(and_57_out), .clk(and_17_out), .Q(d_ff_35_q));  // open: Qn, preset, reset
  and and_57 (and_57_out, and_9_out, not_13_out, d_ff_23_q);
  and and_58 (and_58_out, and_10_out, not_13_out, d_ff_23_q);
  D_Flip_Flop #(.trigger("high")) d_ff_36 (.D(and_58_out), .clk(and_18_out), .Q(d_ff_36_q));  // open: Qn, preset, reset
  or or_3 (or_3_out, and_59_out, and_60_out, and_61_out, and_62_out, and_63_out, and_64_out, and_65_out, and_66_out);
  and and_59 (and_59_out, d_ff_29_q, and_3_out, d_ff_4_q);
  and and_60 (and_60_out, d_ff_30_q, and_4_out, d_ff_4_q);
  and and_61 (and_61_out, d_ff_31_q, and_5_out, d_ff_4_q);
  and and_62 (and_62_out, d_ff_32_q, and_6_out, d_ff_4_q);
  and and_63 (and_63_out, d_ff_33_q, and_7_out, d_ff_4_q);
  and and_64 (and_64_out, d_ff_34_q, and_8_out, d_ff_4_q);
  and and_65 (and_65_out, d_ff_35_q, and_9_out, d_ff_4_q);
  and and_66 (and_66_out, d_ff_36_q, and_10_out, d_ff_4_q);
  and and_67 (and_67_out, and_3_out, not_13_out, d_ff_25_q);
  D_Flip_Flop #(.trigger("high")) d_ff_37 (.D(and_67_out), .clk(and_11_out), .Q(d_ff_37_q));  // open: Qn, preset, reset
  and and_68 (and_68_out, and_4_out, not_13_out, d_ff_25_q);
  D_Flip_Flop #(.trigger("high")) d_ff_38 (.D(and_68_out), .clk(and_12_out), .Q(d_ff_38_q));  // open: Qn, preset, reset
  D_Flip_Flop #(.trigger("high")) d_ff_39 (.D(and_69_out), .clk(and_13_out), .Q(d_ff_39_q));  // open: Qn, preset, reset
  and and_69 (and_69_out, and_5_out, not_13_out, d_ff_25_q);
  D_Flip_Flop #(.trigger("high")) d_ff_40 (.D(and_70_out), .clk(and_14_out), .Q(d_ff_40_q));  // open: Qn, preset, reset
  and and_70 (and_70_out, and_6_out, not_13_out, d_ff_25_q);
  D_Flip_Flop #(.trigger("high")) d_ff_41 (.D(and_71_out), .clk(and_15_out), .Q(d_ff_41_q));  // open: Qn, preset, reset
  and and_71 (and_71_out, and_7_out, not_13_out, d_ff_25_q);
  and and_72 (and_72_out, and_8_out, not_13_out, d_ff_25_q);
  D_Flip_Flop #(.trigger("high")) d_ff_42 (.D(and_72_out), .clk(and_16_out), .Q(d_ff_42_q));  // open: Qn, preset, reset
  and and_73 (and_73_out, and_9_out, not_13_out, d_ff_25_q);
  D_Flip_Flop #(.trigger("high")) d_ff_43 (.D(and_73_out), .clk(and_17_out), .Q(d_ff_43_q));  // open: Qn, preset, reset
  D_Flip_Flop #(.trigger("high")) d_ff_44 (.D(and_74_out), .clk(and_18_out), .Q(d_ff_44_q));  // open: Qn, preset, reset
  and and_74 (and_74_out, and_10_out, not_13_out, d_ff_25_q);
  or or_4 (or_4_out, and_75_out, and_76_out, and_77_out, and_78_out, and_79_out, and_80_out, and_81_out, and_82_out);
  and and_75 (and_75_out, d_ff_37_q, and_3_out, d_ff_4_q);
  and and_76 (and_76_out, d_ff_38_q, and_4_out, d_ff_4_q);
  and and_77 (and_77_out, d_ff_39_q, and_5_out, d_ff_4_q);
  and and_78 (and_78_out, d_ff_40_q, and_6_out, d_ff_4_q);
  and and_79 (and_79_out, d_ff_41_q, and_7_out, d_ff_4_q);
  and and_80 (and_80_out, d_ff_42_q, and_8_out, d_ff_4_q);
  and and_81 (and_81_out, d_ff_43_q, and_9_out, d_ff_4_q);
  and and_82 (and_82_out, d_ff_44_q, and_10_out, d_ff_4_q);
  not not_15 (not_15_out, d_ff_24_q);
  not not_16 (not_16_out, d_ff_26_q);
  not not_17 (not_17_out, d_ff_24_q);
  not not_18 (not_18_out, d_ff_26_q);
  not not_19 (not_19_out, d_ff_27_q);
  not not_20 (not_20_out, d_ff_28_q);
  and and_83 (and_83_out, not_17_out, d_ff_26_q);
  and and_84 (and_84_out, d_ff_24_q, not_18_out);
  and and_85 (and_85_out, d_ff_24_q, d_ff_26_q);
  or or_5 (or_5_out, not_19_out, not_20_out);
  and and_86 (and_86_out, d_ff_24_q, d_ff_26_q, d_ff_27_q, d_ff_28_q);
  not not_21 (not_21_out, undriven);
  not not_22 (not_22_out, undriven_2);
  not not_23 (not_23_out, undriven_3);
  not not_24 (not_24_out, undriven_4);
  and and_87 (and_87_out, not_15_out, not_16_out);
  or or_6 (or_6_out, d_ff_27_q, d_ff_28_q);
  and and_88 (and_88_out, not_21_out, not_22_out, not_23_out, not_24_out);
  and and_89 (and_89_out, and_87_out, or_6_out);
  and and_90 (and_90_out, and_85_out, or_5_out);
  not not_25 (not_25_out, d_ff_28_q);
  not not_26 (not_26_out, d_ff_27_q);
  not not_27 (not_27_out, d_ff_28_q);
  not not_28 (not_28_out, d_ff_27_q);
  not not_29 (not_29_out, d_ff_28_q);
  and and_91 (and_91_out, not_25_out, not_26_out);
  and and_92 (and_92_out, not_27_out, d_ff_27_q);
  and and_93 (and_93_out, d_ff_28_q, not_28_out);
  not not_30 (not_30_out, d_ff_27_q);
  and and_94 (and_94_out, d_ff_28_q, d_ff_27_q);
  and and_95 (and_95_out, and_91_out, d_ff_45_q);
  and and_96 (and_96_out, and_91_out, d_ff_46_q);
  and and_97 (and_97_out, and_91_out, d_ff_47_q);
  and and_98 (and_98_out, and_91_out, d_ff_48_q);
  and and_99 (and_99_out, and_92_out, d_ff_49_q);
  and and_100 (and_100_out, and_92_out, d_ff_50_q);
  and and_101 (and_101_out, and_92_out, d_ff_51_q);
  and and_102 (and_102_out, and_92_out, d_ff_52_q);
  and and_103 (and_103_out, and_93_out, d_ff_45_q);
  and and_104 (and_104_out, and_93_out, d_ff_46_q);
  and and_105 (and_105_out, and_93_out, d_ff_47_q);
  and and_106 (and_106_out, and_93_out, d_ff_48_q);
  and and_107 (and_107_out, and_94_out, d_ff_49_q);
  and and_108 (and_108_out, and_94_out, d_ff_50_q);
  and and_109 (and_109_out, and_94_out, d_ff_51_q);
  and and_110 (and_110_out, and_94_out, d_ff_52_q);
  xor xor_4 (xor_4_out, and_95_out, and_99_out);
  xor xor_5 (xor_5_out, and_96_out, and_100_out);
  xor xor_6 (xor_6_out, and_97_out, and_101_out);
  xor xor_7 (xor_7_out, and_98_out, and_102_out);
  xor xor_8 (xor_8_out, and_103_out, and_107_out);
  xor xor_9 (xor_9_out, and_104_out, and_108_out);
  xor xor_10 (xor_10_out, and_105_out, and_109_out);
  xor xor_11 (xor_11_out, and_106_out, and_110_out);
  and and_111 (and_111_out, and_89_out, not_30_out);
  and and_112 (and_112_out, and_89_out, d_ff_27_q);
  and and_113 (and_113_out, and_83_out, not_29_out);
  and and_114 (and_114_out, and_83_out, d_ff_28_q);
  not not_31 (not_31_out, and_111_out);
  not not_32 (not_32_out, and_111_out);
  not not_33 (not_33_out, and_111_out);
  not not_34 (not_34_out, and_111_out);
  not not_35 (not_35_out, and_112_out);
  not not_36 (not_36_out, and_112_out);
  not not_37 (not_37_out, and_112_out);
  not not_38 (not_38_out, and_112_out);
  not not_39 (not_39_out, and_113_out);
  not not_40 (not_40_out, and_113_out);
  not not_41 (not_41_out, and_113_out);
  not not_42 (not_42_out, and_113_out);
  not not_43 (not_43_out, and_114_out);
  not not_44 (not_44_out, and_114_out);
  not not_45 (not_45_out, and_114_out);
  not not_46 (not_46_out, and_114_out);
  and and_115 (and_115_out, not_31_out, d_ff_45_q);
  and and_116 (and_116_out, and_111_out, undriven_5);
  and and_117 (and_117_out, not_32_out, d_ff_46_q);
  and and_118 (and_118_out, and_111_out, undriven_7);
  and and_119 (and_119_out, not_33_out, d_ff_47_q);
  and and_120 (and_120_out, and_111_out, undriven_9);
  and and_121 (and_121_out, not_34_out, d_ff_48_q);
  and and_122 (and_122_out, and_111_out, undriven_11);
  and and_123 (and_123_out, not_35_out, d_ff_49_q);
  and and_124 (and_124_out, and_112_out, undriven_6);
  and and_125 (and_125_out, not_36_out, d_ff_50_q);
  and and_126 (and_126_out, and_112_out, undriven_8);
  and and_127 (and_127_out, not_37_out, d_ff_51_q);
  and and_128 (and_128_out, and_112_out, undriven_10);
  and and_129 (and_129_out, not_38_out, d_ff_52_q);
  and and_130 (and_130_out, and_112_out, undriven_12);
  and and_131 (and_131_out, not_39_out, d_ff_53_q);
  and and_132 (and_132_out, and_113_out, xor_4_out);
  and and_133 (and_133_out, not_40_out, d_ff_54_q);
  and and_134 (and_134_out, and_113_out, xor_5_out);
  and and_135 (and_135_out, not_41_out, d_ff_55_q);
  and and_136 (and_136_out, and_113_out, xor_6_out);
  and and_137 (and_137_out, not_42_out, d_ff_56_q);
  and and_138 (and_138_out, and_113_out, xor_7_out);
  and and_139 (and_139_out, not_43_out, d_ff_57_q);
  and and_140 (and_140_out, and_114_out, xor_8_out);
  and and_141 (and_141_out, not_44_out, d_ff_58_q);
  and and_142 (and_142_out, and_114_out, xor_9_out);
  and and_143 (and_143_out, not_45_out, d_ff_59_q);
  and and_144 (and_144_out, and_114_out, xor_10_out);
  and and_145 (and_145_out, not_46_out, d_ff_60_q);
  and and_146 (and_146_out, and_114_out, xor_11_out);
  or or_7 (or_7_out, and_121_out, and_122_out);
  or or_8 (or_8_out, and_129_out, and_130_out);
  or or_9 (or_9_out, and_137_out, and_138_out);
  or or_10 (or_10_out, and_145_out, and_146_out);
  or or_11 (or_11_out, and_115_out, and_116_out);
  or or_12 (or_12_out, and_117_out, and_118_out);
  or or_13 (or_13_out, and_119_out, and_120_out);
  or or_14 (or_14_out, and_123_out, and_124_out);
  or or_15 (or_15_out, and_125_out, and_126_out);
  or or_16 (or_16_out, and_127_out, and_128_out);
  or or_17 (or_17_out, and_131_out, and_132_out);
  or or_18 (or_18_out, and_133_out, and_134_out);
  or or_19 (or_19_out, and_135_out, and_136_out);
  or or_20 (or_20_out, and_139_out, and_140_out);
  or or_21 (or_21_out, and_141_out, and_142_out);
  or or_22 (or_22_out, and_143_out, and_144_out);
  D_Flip_Flop d_ff_45 (.D(or_11_out), .clk(clock_1_out), .Q(d_ff_45_q));  // open: Qn, preset, reset
  D_Flip_Flop d_ff_46 (.D(or_12_out), .clk(clock_1_out), .Q(d_ff_46_q));  // open: Qn, preset, reset
  D_Flip_Flop d_ff_47 (.D(or_13_out), .clk(clock_1_out), .Q(d_ff_47_q));  // open: Qn, preset, reset
  D_Flip_Flop d_ff_48 (.D(or_7_out), .clk(clock_1_out), .Q(d_ff_48_q));  // open: Qn, preset, reset
  D_Flip_Flop d_ff_49 (.D(or_14_out), .clk(clock_1_out), .Q(d_ff_49_q));  // open: Qn, preset, reset
  D_Flip_Flop d_ff_50 (.D(or_15_out), .clk(clock_1_out), .Q(d_ff_50_q));  // open: Qn, preset, reset
  D_Flip_Flop d_ff_51 (.D(or_16_out), .clk(clock_1_out), .Q(d_ff_51_q));  // open: Qn, preset, reset
  D_Flip_Flop d_ff_52 (.D(or_8_out), .clk(clock_1_out), .Q(d_ff_52_q));  // open: Qn, preset, reset
  D_Flip_Flop d_ff_53 (.D(or_17_out), .clk(clock_1_out), .Q(d_ff_53_q));  // open: Qn, preset, reset
  D_Flip_Flop d_ff_54 (.D(or_18_out), .clk(clock_1_out), .Q(d_ff_54_q));  // open: Qn, preset, reset
  D_Flip_Flop d_ff_55 (.D(or_19_out), .clk(clock_1_out), .Q(d_ff_55_q));  // open: Qn, preset, reset
  D_Flip_Flop d_ff_56 (.D(or_9_out), .clk(clock_1_out), .Q(d_ff_56_q));  // open: Qn, preset, reset
  D_Flip_Flop d_ff_57 (.D(or_20_out), .clk(clock_1_out), .Q(d_ff_57_q));  // open: Qn, preset, reset
  D_Flip_Flop d_ff_58 (.D(or_21_out), .clk(clock_1_out), .Q(d_ff_58_q));  // open: Qn, preset, reset
  D_Flip_Flop d_ff_59 (.D(or_22_out), .clk(clock_1_out), .Q(d_ff_59_q));  // open: Qn, preset, reset
  D_Flip_Flop d_ff_60 (.D(or_10_out), .clk(clock_1_out), .Q(d_ff_60_q));  // open: Qn, preset, reset

  // Notes on the sheet:
  //   ADD 1
  //   3-bit address input pins
  //   PROGRAM COUNTER
  //   Mode input pin
  //   STOP INCREMENTING
  //   4-bit data input pins
  //   INSTRUCTION REGISTER
  //   INSTRUCTION RAM
  //   LSB
  //   MSB
  //   00--load
  //    01--save
  //   10--add
  //   11--sub
  //   HALT
  //   SPECIAL CASES : TBD
  //   JUMP
  //   IDENTIFY OPCODE
  //   IDENTIFY DEST REG
  //   MEMORY SRC OR OTHER REG
  //   A
  //   Sub
  //   CONTROL UNIT
  //   Save
  //   L
  //   FROM R0
  //   FROM R1
  //   REGISTER BLOCK
  //   DATA RAM
endmodule
